# Fritzing sketch Gif_Box_Led (saved by Fritzing 0.9.1b)
breadboards: 1

parts:
  Bauteil1 = Arduino Nano (Rev3.0)
  J3 = female pin header, 3 pins [form="♀ (female)"]
  R1 = Resistor [tolerance=±5% resistance=220 package=THT]
  J4 = Generic female header - 8 pins [form="♀ (female)" package=THT]

nets:
  N1: Bauteil1.GND, J4.GND#0
  N2: Bauteil1.D9, R1.Pin_0
  N3: Bauteil1.D10, J4.CS
  N4: Bauteil1.D11/MOSI, J4.MOSI
  N5: Bauteil1.D12/MISO, J4.MISO
  N6: Bauteil1.3V3, J4.3_3V
  N7: Bauteil1.D13/SCK, J4.SCK
  N8: J3.pin1, R1.Pin_1

custom parts:
  Generic female header - 8 pins: Generic female header
